// Logisim project s-mips.circ as structural Verilog: 8 circuits, main circuit S-MIPS Board
module S_MIPS_Board (
  input  DESHABILITAR_DISPATCHER,
  output halt
);

  wire button_1_out, CLK, CS, d_ff_1_q, LCLR, LoadRAM, LoadRAMOn, LW, R_R_W, R_W, ram_dispatcher_1_finished,
       RCS, Reset_out, RST, TTY_EN;
  wire [2:0] KDB;
  wire [3:0] LMask, Mask, ram_1_read_time, ram_1_write_time, RMask;
  wire [6:0] KDB_DATA, TTY_DATA;
  wire [15:0] Addr, LAddr, RAddr;
  wire [31:0] I0, I1, I2, I3, LData, ram_1_data_out_0, ram_1_data_out_1, ram_1_data_out_2, ram_1_data_out_3,
       RI0, RI1, RI2, RI3;

  TTY #(.rows(25), .cols(80)) tty_1 (.data(TTY_DATA), .clk(CLK), .we(TTY_EN), .clr(RST));
  not not_1 (LoadRAMOn, ram_dispatcher_1_finished);
  RAM_Dispatcher ram_dispatcher_1 (
    .WriteTime(ram_1_write_time), .Clock(CLK), .Data(LData), .Address(LAddr), .Mask(LMask),
    .Finished(ram_dispatcher_1_finished), .Write(LW), .CLR(LCLR));
  Keyboard #(.buflen(64)) keyboard_1 (.clk(CLK), .re(KDB[0]), .avail(KDB[2]), .data(KDB_DATA));  // open: clr
  RAM ram_1 (
    .Address(RAddr), .Data_Out_0(ram_1_data_out_0), .Data_Out_1(ram_1_data_out_1),
    .Data_Out_2(ram_1_data_out_2), .Data_Out_3(ram_1_data_out_3), .Data_In_0(RI0), .Data_In_1(RI1),
    .Data_In_2(RI2), .Data_In_3(RI3), .Mask(RMask), .nRead_Write(R_R_W), .Chip_Select(RCS),
    .Read_Time(ram_1_read_time), .Reset(button_1_out), .Write_Time(ram_1_write_time));
  Button button_1 (.out(button_1_out));
  D_Flip_Flop d_ff_1 (.clk(CLK), .D(1'b1), .Q(d_ff_1_q), .reset(Reset_out));  // open: Qn, preset, en
  Button Reset (.out(Reset_out));
  S_MIPS s_mips_1 (
    .Kbd_Enable(KDB[0]), .Address(Addr), .Kbd_Clear(KDB[1]), .Kbd_Available(KDB[2]), .RAM_In_0(I0),
    .Kbd_ASCII_Data(KDB_DATA), .RAM_In_1(I1), .TTY_Enable(TTY_EN), .RAM_In_2(I2), .RAM_In_3(I2),
    .TTY_ASCII_Data(TTY_DATA), .Reset(RST), .RAM_Out_0(ram_1_data_out_0), .Clock(CLK),
    .RAM_Out_1(ram_1_data_out_1), .Stop(halt), .RAM_Out_2(ram_1_data_out_2), .RAM_Out_3(ram_1_data_out_3),
    .Mask(Mask), .Read_Time(ram_1_read_time), .Write_Time(ram_1_write_time), .nRead_Write(R_W),
    .Chip_Select(CS));
  D_Flip_Flop d_ff_2 (.clk(CLK), .D(d_ff_1_q), .Qn(LCLR), .reset(Reset_out));  // open: Q, preset, en
  or or_1 (RST, LCLR, LoadRAM);
  Clock clock_1 (.out(CLK));
  Multiplexer #(.width(32), .enable("false")) multiplexer_1 (.in0(I0), .in1(LData), .out(RI0), .sel(LoadRAM));
  Multiplexer #(.width(32), .enable("false")) multiplexer_2 (.in0(I1), .in1(LData), .out(RI1), .sel(LoadRAM));
  Multiplexer #(.width(32), .enable("false")) multiplexer_3 (.in0(I2), .in1(LData), .out(RI2), .sel(LoadRAM));
  Multiplexer #(.width(32), .enable("false")) multiplexer_4 (.in0(I3), .in1(LData), .out(RI3), .sel(LoadRAM));
  and and_1 (LoadRAM, ~DESHABILITAR_DISPATCHER, LoadRAMOn);  // AND_Gate
  Multiplexer #(.width(16), .enable("false")) multiplexer_5 (.in0(Addr), .in1(LAddr), .out(RAddr), .sel(LoadRAM));
  Multiplexer #(.width(4), .enable("false")) multiplexer_6 (.in0(Mask), .in1(LMask), .out(RMask), .sel(LoadRAM));
  Multiplexer #(.enable("false")) multiplexer_7 (.in0(CS), .in1(LW), .out(RCS), .sel(LoadRAM));
  Multiplexer #(.enable("false")) multiplexer_8 (.in0(R_W), .in1(LW), .out(R_R_W), .sel(LoadRAM));

  // Notes on the sheet:
  //   NO MODIFICAR
  //   Keyboard
endmodule

module RAM (
  input  [15:0] Address,
  input  [31:0] Data_In_0,
  input  [31:0] Data_In_1,
  input  [31:0] Data_In_2,
  input  [31:0] Data_In_3,
  input  [3:0] Mask,
  input  nRead_Write,
  input  Chip_Select,
  input  Reset,
  output [31:0] Data_Out_0,
  output [31:0] Data_Out_1,
  output [31:0] Data_Out_2,
  output [31:0] Data_Out_3,
  output [3:0] Read_Time,
  output [3:0] Write_Time
);

  wire and_2_out, and_3_out, and_4_out, and_5_out, and_6_out, and_7_out, and_8_out, and_9_out, Changed, CLK,
       comparator_2_eq, comparator_3_eq, comparator_4_eq, comparator_5_eq, comparator_6_eq, Count,
       demultiplexer_3_out0, Idle, Idle_q, Load, Load0, Load1, nand_1_out, or_1_out, or_2_out, or_3_out,
       or_4_out, or_5_out, or_6_out, or_7_out, or_8_out, or_9_out, or_10_out, Proc_q, Update_Mem, Zero_Time;
  wire [3:0] counter_1_q, multiplexer_1_out, subtractor_1_out;
  wire [31:0] register_1_q, register_2_q, register_3_q, register_4_q, register_5_q;

  // Probe on 4'b0011
  // Probe on 4'b0010
  Multiplexer #(.width(4), .enable("false")) multiplexer_1 (
    .in0(4'b0011), .in1(4'b0010), .out(multiplexer_1_out), .sel(nRead_Write));
  or or_1 (or_1_out, Idle, Update_Mem);
  or or_2 (or_2_out, ~Chip_Select, Reset);  // OR_Gate
  Subtractor #(.width(4)) subtractor_1 (.a(multiplexer_1_out), .b(4'b0010), .out(subtractor_1_out));  // open: bin, bout
  Demultiplexer #(.enable("false")) demultiplexer_1 (.out0(Idle), .out1(Load0), .in(Idle_q), .sel(Changed));
  D_Flip_Flop u_Idle (.clk(CLK), .D(or_1_out), .Q(Idle_q), .preset(or_2_out));  // open: Qn, en, reset
  // Probe on counter_1_q
  Counter #(.width(4), .max('hf)) counter_1 (
    .load(Load), .D(subtractor_1_out), .count(Count), .Q(counter_1_q), .clk(CLK), .clr(or_3_out));  // open: carry
  or or_3 (or_3_out, ~Chip_Select, Reset);  // OR_Gate
  Comparator #(.width(4), .mode("unsigned")) comparator_1 (
    .a(4'b0000), .b(counter_1_q), .eq(Zero_Time));  // open: gt, lt
  or or_4 (or_4_out, Count, Load0, Load1);
  Register #(.width(32)) register_1 (.D(Data_In_0), .en(Chip_Select), .Q(register_1_q), .clk(CLK), .clr(or_5_out));
  or or_5 (or_5_out, ~Chip_Select, Reset);  // OR_Gate
  Register #(.width(32)) register_2 (.D(Data_In_1), .en(Chip_Select), .Q(register_2_q), .clk(CLK), .clr(or_6_out));
  or or_6 (or_6_out, ~Chip_Select, Reset);  // OR_Gate
  Register #(.width(32)) register_3 (.D(Data_In_2), .en(Chip_Select), .Q(register_3_q), .clk(CLK), .clr(or_7_out));
  or or_7 (or_7_out, ~Chip_Select, Reset);  // OR_Gate
  Register #(.width(32)) register_4 (.D(Data_In_3), .en(Chip_Select), .Q(register_4_q), .clk(CLK), .clr(or_8_out));
  or or_8 (or_8_out, ~Chip_Select, Reset);  // OR_Gate
  Register #(.width(32)) register_5 (
    .D({{11{1'b1}}, nRead_Write, Mask, Address}), .en(Chip_Select), .Q(register_5_q), .clk(CLK),
    .clr(or_9_out));
  or or_9 (or_9_out, ~Chip_Select, Reset);  // OR_Gate
  D_Flip_Flop Proc (.clk(CLK), .D(or_4_out), .Q(Proc_q), .reset(or_10_out));  // open: Qn, preset, en
  or or_10 (or_10_out, ~Chip_Select, Reset);  // OR_Gate
  Demultiplexer #(.enable("false")) demultiplexer_2 (
    .out0(Count), .out1(Update_Mem), .in(demultiplexer_3_out0), .sel(Zero_Time));
  Demultiplexer #(.enable("false")) demultiplexer_3 (
    .out0(demultiplexer_3_out0), .out1(Load1), .in(Proc_q), .sel(Changed));
  Clock clock_1 (.out(CLK));
  Comparator #(.width(32)) comparator_2 (.a(register_1_q), .b(Data_In_0), .eq(comparator_2_eq));  // open: gt, lt
  Comparator #(.width(32)) comparator_3 (.a(register_2_q), .b(Data_In_1), .eq(comparator_3_eq));  // open: gt, lt
  Comparator #(.width(32)) comparator_4 (.a(register_3_q), .b(Data_In_2), .eq(comparator_4_eq));  // open: gt, lt
  Comparator #(.width(32)) comparator_5 (.a(register_4_q), .b(Data_In_3), .eq(comparator_5_eq));  // open: gt, lt
  Comparator #(.width(32)) comparator_6 (
    .a(register_5_q), .b({{11{1'b1}}, nRead_Write, Mask, Address}), .eq(comparator_6_eq));  // open: gt, lt
  nand nand_1 (nand_1_out, comparator_6_eq, comparator_2_eq, comparator_3_eq, comparator_4_eq, comparator_5_eq);
  and and_1 (Changed, nand_1_out, Chip_Select);
  or or_11 (Load, Count, Load1, Load0);
  and and_2 (and_2_out, Mask[0], Update_Mem, nRead_Write);
  and and_3 (and_3_out, Mask[1], Update_Mem, nRead_Write);
  and and_4 (and_4_out, Mask[2], Update_Mem, nRead_Write);
  and and_5 (and_5_out, Mask[3], Update_Mem, nRead_Write);
  RAM_part #(.addrWidth(16), .dataWidth(32), .bus("separate")) ram_1 (
    .addr(Address), .din(Data_In_0), .data(Data_Out_0), .str(and_2_out), .sel(Chip_Select), .clk(CLK),
    .ld(and_6_out), .clr(Reset));
  and and_6 (and_6_out, ~nRead_Write, Idle);  // AND_Gate
  RAM_part #(.addrWidth(16), .dataWidth(32), .bus("separate")) ram_2 (
    .addr(Address), .din(Data_In_1), .data(Data_Out_1), .str(and_3_out), .sel(Chip_Select), .clk(CLK),
    .ld(and_7_out), .clr(Reset));
  and and_7 (and_7_out, ~nRead_Write, Idle);  // AND_Gate
  RAM_part #(.addrWidth(16), .dataWidth(32), .bus("separate")) ram_3 (
    .addr(Address), .din(Data_In_2), .data(Data_Out_2), .str(and_4_out), .sel(Chip_Select), .clk(CLK),
    .ld(and_8_out), .clr(Reset));
  and and_8 (and_8_out, ~nRead_Write, Idle);  // AND_Gate
  RAM_part #(.addrWidth(16), .dataWidth(32), .bus("separate")) ram_4 (
    .addr(Address), .din(Data_In_3), .data(Data_Out_3), .str(and_5_out), .sel(Chip_Select), .clk(CLK),
    .ld(and_9_out), .clr(Reset));
  and and_9 (and_9_out, ~nRead_Write, Idle);  // AND_Gate

  assign Read_Time = 4'b0011;
  assign Write_Time = 4'b0010;

  // Other names for the same wires on the sheet: M0 = Mask[0]; M1 = Mask[1]; M2 = Mask[2]; M3 = Mask[3];
  //   RW = nRead_Write; CLR = Reset; CS = Chip_Select; Load2 = Count

  // Notes on the sheet:
  //   NO MODIFICAR
  //   excepto quizás los valores RT y WT
  //   BANK0
  //   BANK1
  //   BANK2
  //   BANK3
endmodule

module S_MIPS (
  input  Kbd_Available,
  input  [6:0] Kbd_ASCII_Data,
  input  [31:0] RAM_Out_0,
  input  [31:0] RAM_Out_1,
  input  Reset,
  input  [31:0] RAM_Out_2,
  input  Clock,
  input  [31:0] RAM_Out_3,
  input  [3:0] Read_Time,
  input  [3:0] Write_Time,
  output Kbd_Enable,
  output [15:0] Address,
  output Kbd_Clear,
  output TTY_Enable,
  output [6:0] TTY_ASCII_Data,
  output Stop,
  output [31:0] RAM_In_0,
  output [31:0] RAM_In_1,
  output [31:0] RAM_In_2,
  output [31:0] RAM_In_3,
  output [3:0] Mask,
  output nRead_Write,
  output Chip_Select
);

  wire Next;
  wire [4:0] instruction_decoder_1_out_3, instruction_decoder_1_out_4, instruction_decoder_1_out_5;
  wire [15:0] undriven;
  wire [31:0] ram_out_select_1_out_8;

  Button button_1 (.out(Next));
  Register #(.width(16)) register_1 (.D(undriven), .Q(Address), .clk(Clock), .clr(Reset));  // open: en
  RAM_Out_Select ram_out_select_1 (
    .RAM_Out_0(RAM_Out_0), .RAM_Out_1(RAM_Out_1), .RAM_Out_2(RAM_Out_2), .RAM_Out_3(RAM_Out_3), .Next(Next),
    .CLK(Clock), .out_8(ram_out_select_1_out_8), .RST(Reset));
  Instruction_Decoder instruction_decoder_1 (
    .Instruction(ram_out_select_1_out_8), .out_3(instruction_decoder_1_out_3),
    .out_4(instruction_decoder_1_out_4), .out_5(instruction_decoder_1_out_5));  // open: out_2, out_6, out_7
  Register_File register_file_1 (
    .in_1(Clock), .in_3(instruction_decoder_1_out_5), .in_5(instruction_decoder_1_out_3),
    .in_6(instruction_decoder_1_out_4), .in_7(Reset));  // open: in_2, in_4, out_8, out_9

  assign nRead_Write = 1'b0;

  // Other names for the same wires on the sheet: CLK = Clock; CLR = Reset; CS = Chip_Select;
  //   KBD_AVAIL = Kbd_Available; KBD_CLR = Kbd_Clear; KBD_DATA[6:0] = Kbd_ASCII_Data; RAM_A[15:0] = Address;
  //   RAM_INPUT_0[31:0] = RAM_In_0; RAM_INPUT_1[31:0] = RAM_In_1; RAM_INPUT_2[31:0] = RAM_In_2;
  //   RAM_INPUT_3[31:0] = RAM_In_3; RAM_MASK[3:0] = Mask; RAM_OUTPUT_0[31:0] = RAM_Out_0;
  //   RAM_OUTPUT_1[31:0] = RAM_Out_1; RAM_OUTPUT_2[31:0] = RAM_Out_2; RAM_OUTPUT_3[31:0] = RAM_Out_3;
  //   TTY_DATA[6:0] = TTY_ASCII_Data

  // Notes on the sheet:
  //   RAM ADDRESS
  //   DATA FROM RAM
  //   DATA TO RAM
  //   DATA WRITE MASK
  //   RAM TIMING
  //   RAM CONTROL
  //   KEYBOARD
  //   TTY
  //   SEQUENCING
endmodule

module RAM_Dispatcher (
  input  [3:0] WriteTime,
  input  Clock,
  input  CLR,
  output [31:0] Data,
  output [15:0] Address,
  output [3:0] Mask,
  output Finished,
  output Write
);

  wire demultiplexer_2_out1, demultiplexer_3_out1, End, IDLE_q, IncAddr, Load, or_1_out, or_2_out, While_q,
       WriteEnd;
  wire [3:0] counter_1_q;
  wire [31:0] CurrentAddress_q;

  Counter #(.width(32), .max('hffffffff)) CurrentAddress (
    .count(IncAddr), .Q({CurrentAddress_q[31:18], Address, CurrentAddress_q[1:0]}), .clk(Clock), .clr(CLR));  // open: load, D, carry
  or or_1 (or_1_out, IncAddr, demultiplexer_3_out1, Finished);
  D_Flip_Flop IDLE (.clk(Clock), .D(or_1_out), .Q(IDLE_q), .preset(CLR));  // open: Qn, en, reset
  Demultiplexer #(.enable("false")) demultiplexer_1 (.out0(Load), .out1(Finished), .in(IDLE_q), .sel(End));
  D_Flip_Flop While (.clk(Clock), .D(or_2_out), .Q(While_q), .reset(CLR));  // open: Qn, preset, en
  or or_2 (or_2_out, Write, Load);
  RAM_part #(.addrWidth(18), .dataWidth(32)) ram_1 (
    .addr({Address, CurrentAddress_q[1:0]}), .data(Data), .clk(Clock));  // open: sel, ld, clr
  Demultiplexer #(.enable("false")) demultiplexer_2 (
    .out0(Write), .out1(demultiplexer_2_out1), .in(While_q), .sel(WriteEnd));
  Decoder #(.select(2)) decoder_1 (
    .out0(Mask[0]), .out1(Mask[1]), .out2(Mask[2]), .out3(Mask[3]), .sel(CurrentAddress_q[1:0]));  // open: en
  Demultiplexer #(.enable("false")) demultiplexer_3 (
    .out0(IncAddr), .out1(demultiplexer_3_out1), .in(demultiplexer_2_out1), .sel(End));
  Counter #(.width(4), .max('hf)) counter_1 (
    .load(Load), .D(WriteTime), .count(Write), .Q(counter_1_q), .clk(Clock));  // open: carry, clr
  Comparator #(.width(32)) comparator_1 (.a(Data), .b({32{1'b1}}), .eq(End));  // open: gt, lt
  Comparator #(.width(4)) comparator_2 (.a(4'b0000), .b(counter_1_q), .eq(WriteEnd));  // open: gt, lt

  // Other names for the same wires on the sheet: CLK = Clock; Count = Write; WT[3:0] = WriteTime
endmodule

module Branch_Control (
  input  [15:0] in_1,
  output [15:0] out_2
);

  Adder #(.width(16)) adder_1 (.a(16'h4), .b(in_1), .out(out_2));  // open: cin, cout

  // Other names for the same wires on the sheet: Curr_Addr[15:0] = in_1
endmodule

module RAM_Out_Select (
  input  [31:0] RAM_Out_0,
  input  [31:0] RAM_Out_1,
  input  [31:0] RAM_Out_2,
  input  [31:0] RAM_Out_3,
  input  Next,
  input  CLK,
  input  RST,
  output [31:0] out_8
);

  wire [1:0] counter_1_q;

  Counter #(.width(2), .max('h3)) counter_1 (
    .count(Next), .Q(counter_1_q), .clk(CLK), .clr(RST));  // open: load, D, carry
  Multiplexer #(.select(2), .width(32)) multiplexer_1 (
    .in0(RAM_Out_0), .in1(RAM_Out_1), .in2(RAM_Out_2), .in3(RAM_Out_3), .out(out_8), .sel(counter_1_q));  // open: en
endmodule

module Instruction_Decoder (
  input  [31:0] Instruction,
  output [5:0] out_2,
  output [4:0] out_3,
  output [4:0] out_4,
  output [4:0] out_5,
  output [5:0] out_6,
  output [10:0] out_7
);

  // Probe on {Instruction[16], Instruction[17], Instruction[18], Instruction[31:24]}

  assign out_2 = Instruction[7:2];
  assign out_3 = {Instruction[1:0], Instruction[15:13]};
  assign out_4 = Instruction[12:8];
  assign out_5 = Instruction[23:19];
  assign out_6 = Instruction[29:24];
  assign out_7 = {Instruction[16], Instruction[17], Instruction[18], Instruction[31:24]};

  // Other names for the same wires on the sheet: Const[10:0] = {Instruction[16], Instruction[17], Instruction[18], Instruction[31:24]};
  //   FUNC_CODE[5:0] = Instruction[29:24];
  //   X[4:0] = {Instruction[16], Instruction[17], Instruction[18], Instruction[31:30]};
  //   OPCODE[5:0] = Instruction[7:2]; RD[4:0] = Instruction[23:19]; RS[4:0] = {Instruction[1:0], Instruction[15:13]};
  //   RT[4:0] = Instruction[12:8]
endmodule

module Register_File (
  input  in_1,
  input  in_2,
  input  [4:0] in_3,
  input  [31:0] in_4,
  input  [4:0] in_5,
  input  [4:0] in_6,
  input  in_7,
  output [31:0] out_8,
  output [31:0] out_9
);

  wire w00, w0A, w0B, w0C, w0D, w0E, w0F, w01, w1A, w1B, w1C, w1D, w1E, w1F, w02, w03, w04, w05, w06, w07,
       w08, w09, w10, w11, w12, w13, w14, w15, w16, w17, w18, w19;
  wire [31:0] r00, r0A, r0B, r0C, r0D, r0E, r0F, r01, r1A, r1B, r1C, r1D, r1E, r1F, r02, r03, r04, r05, r06,
       r07, r08, r09, r10, r11, r12, r13, r14, r15, r16, r17, r18, r19;

  Decoder #(.select(5), .disabled(0)) decoder_1 (
    .out0(w00), .out1(w01), .out2(w02), .out3(w03), .out4(w04), .out5(w05), .out6(w06), .out7(w07),
    .out8(w08), .out9(w09), .out10(w0A), .out11(w0B), .out12(w0C), .out13(w0D), .out14(w0E), .out15(w0F),
    .out16(w10), .out17(w11), .out18(w12), .out19(w13), .out20(w14), .out21(w15), .out22(w16), .out23(w17),
    .out24(w18), .out25(w19), .out26(w1A), .out27(w1B), .out28(w1C), .out29(w1D), .out30(w1E), .out31(w1F),
    .sel(in_3), .en(in_2));
  Register #(.width(32)) register_1 (.D(in_4), .en(w00), .Q(r00), .clk(in_1), .clr(in_7));
  Register #(.width(32)) register_2 (.D(in_4), .en(w04), .Q(r04), .clk(in_1), .clr(in_7));
  Register #(.width(32)) register_3 (.D(in_4), .en(w08), .Q(r08), .clk(in_1), .clr(in_7));
  Register #(.width(32)) register_4 (.D(in_4), .en(w0C), .Q(r0C), .clk(in_1), .clr(in_7));
  Register #(.width(32)) register_5 (.D(in_4), .en(w10), .Q(r10), .clk(in_1), .clr(in_7));
  Register #(.width(32)) register_6 (.D(in_4), .en(w14), .Q(r14), .clk(in_1), .clr(in_7));
  Register #(.width(32)) register_7 (.D(in_4), .en(w18), .Q(r18), .clk(in_1), .clr(in_7));
  Register #(.width(32)) register_8 (.D(in_4), .en(w1C), .Q(r1C), .clk(in_1), .clr(in_7));
  Register #(.width(32)) register_9 (.D(in_4), .en(w01), .Q(r01), .clk(in_1), .clr(in_7));
  Register #(.width(32)) register_10 (.D(in_4), .en(w05), .Q(r05), .clk(in_1), .clr(in_7));
  Register #(.width(32)) register_11 (.D(in_4), .en(w09), .Q(r09), .clk(in_1), .clr(in_7));
  Register #(.width(32)) register_12 (.D(in_4), .en(w0D), .Q(r0D), .clk(in_1), .clr(in_7));
  Register #(.width(32)) register_13 (.D(in_4), .en(w11), .Q(r11), .clk(in_1), .clr(in_7));
  Register #(.width(32)) register_14 (.D(in_4), .en(w15), .Q(r15), .clk(in_1), .clr(in_7));
  Register #(.width(32)) register_15 (.D(in_4), .en(w19), .Q(r19), .clk(in_1), .clr(in_7));
  Register #(.width(32)) register_16 (.D(in_4), .en(w1D), .Q(r1D), .clk(in_1), .clr(in_7));
  Register #(.width(32)) register_17 (.D(in_4), .en(w02), .Q(r02), .clk(in_1), .clr(in_7));
  Register #(.width(32)) register_18 (.D(in_4), .en(w06), .Q(r06), .clk(in_1), .clr(in_7));
  Register #(.width(32)) register_19 (.D(in_4), .en(w0A), .Q(r0A), .clk(in_1), .clr(in_7));
  Register #(.width(32)) register_20 (.D(in_4), .en(w0E), .Q(r0E), .clk(in_1), .clr(in_7));
  Register #(.width(32)) register_21 (.D(in_4), .en(w12), .Q(r12), .clk(in_1), .clr(in_7));
  Register #(.width(32)) register_22 (.D(in_4), .en(w16), .Q(r16), .clk(in_1), .clr(in_7));
  Register #(.width(32)) register_23 (.D(in_4), .en(w1A), .Q(r1A), .clk(in_1), .clr(in_7));
  Register #(.width(32)) register_24 (.D(in_4), .en(w1E), .Q(r1E), .clk(in_1), .clr(in_7));
  Register #(.width(32)) register_25 (.D(in_4), .en(w03), .Q(r03), .clk(in_1), .clr(in_7));
  Register #(.width(32)) register_26 (.D(in_4), .en(w07), .Q(r07), .clk(in_1), .clr(in_7));
  Register #(.width(32)) register_27 (.D(in_4), .en(w0B), .Q(r0B), .clk(in_1), .clr(in_7));
  Register #(.width(32)) register_28 (.D(in_4), .en(w0F), .Q(r0F), .clk(in_1), .clr(in_7));
  Register #(.width(32)) register_29 (.D(in_4), .en(w13), .Q(r13), .clk(in_1), .clr(in_7));
  Register #(.width(32)) register_30 (.D(in_4), .en(w17), .Q(r17), .clk(in_1), .clr(in_7));
  Register #(.width(32)) register_31 (.D(in_4), .en(w1B), .Q(r1B), .clk(in_1), .clr(in_7));
  Register #(.width(32)) register_32 (.D(in_4), .en(w1F), .Q(r1F), .clk(in_1), .clr(in_7));
  Multiplexer #(.select(5), .width(32), .disabled(0), .enable("false")) multiplexer_1 (
    .in0(r00), .in1(r01), .in2(r02), .in3(r03), .in4(r04), .in5(r05), .in6(r06), .in7(r07), .in8(r08),
    .in9(r09), .in10(r0A), .in11(r0B), .in12(r0C), .in13(r0D), .in14(r0E), .in15(r0F), .in16(r10),
    .in17(r11), .in18(r12), .in19(r13), .in20(r14), .in21(r15), .in22(r16), .in23(r17), .in24(r18),
    .in25(r19), .in26(r1A), .in27(r1B), .in28(r1C), .in29(r1D), .in30(r1E), .in31(r1F), .out(out_8),
    .sel(in_5));
  Multiplexer #(.select(5), .width(32), .disabled(0), .enable("false")) multiplexer_2 (
    .in0(r00), .in1(r01), .in2(r02), .in3(r03), .in4(r04), .in5(r05), .in6(r06), .in7(r07), .in8(r08),
    .in9(r09), .in10(r0A), .in11(r0B), .in12(r0C), .in13(r0D), .in14(r0E), .in15(r0F), .in16(r10),
    .in17(r11), .in18(r12), .in19(r13), .in20(r14), .in21(r15), .in22(r16), .in23(r17), .in24(r18),
    .in25(r19), .in26(r1A), .in27(r1B), .in28(r1C), .in29(r1D), .in30(r1E), .in31(r1F), .out(out_9),
    .sel(in_6));
  // Probe on out_8
  // Probe on out_9

  // Other names for the same wires on the sheet: RS[4:0] = in_5; rst = in_7; RT[4:0] = in_6; T = in_1; w = in_2;
  //   write[31:0] = in_4
endmodule
